# Fritzing sketch LED (saved by Fritzing 0.9.4)
breadboards: 1

parts:
  VCC2 = Battery
  R2 = Resistor [tolerance=±5% resistance=220 package="2512 [SMD]"]
  LED2 = smd LED [color="Red (633nm)" package="1206 [SMD]"]

nets:
  N1: VCC2.-, LED2.cathode
  N2: VCC2.+, R2.Pin_1
  N3: R2.Pin_0, LED2.anode
