# Fritzing sketch SN7414 chip (saved by Fritzing 0.9.4)
breadboards: 1

parts:
  VCC1 = Battery
  U1 = SN74LS14N [package="DIP14 [THT]"]
  LED1 = smd LED [color="Red (633nm)" package="1206 [SMD]"]
  R1 = Resistor [tolerance=±5% resistance=220 package=THT]

nets:
  N1: VCC1.-, U1.GND, R1.Pin_1
  N2: VCC1.+, U1.1A, U1.VCC
  N3: U1.1Y, U1.2A
  N4: U1.2Y, U1.3A
  N5: U1.3Y, U1.6A
  N6: U1.4Y, LED1.anode
  N7: U1.4A, U1.5Y
  N8: U1.5A, U1.6Y
  N9: LED1.cathode, R1.Pin_0
