// Logisim project adder-subtractor.circ as structural Verilog: 2 circuits, main circuit main
module main (
  input  B3,
  input  A3,
  input  B2,
  input  A2,
  input  B1,
  input  A1,
  input  B0,
  input  A0,
  input  Cin,
  output carry_out,
  output S3,
  output S2,
  output S1,
  output S0
);

  wire full_adder_2_cout, full_adder_3_cout, full_adder_4_cout, xor_1_out, xor_2_out, xor_3_out, xor_4_out;

  xor xor_1 (xor_1_out, Cin, B3);
  Full_adder full_adder_1 (.A(xor_1_out), .B(A3), .Cout(carry_out), .Cin(full_adder_2_cout), .Sum(S3));
  xor xor_2 (xor_2_out, Cin, B2);
  Full_adder full_adder_2 (.A(xor_2_out), .B(A2), .Cout(full_adder_2_cout), .Cin(full_adder_3_cout), .Sum(S2));
  xor xor_3 (xor_3_out, Cin, B1);
  Full_adder full_adder_3 (.A(xor_3_out), .B(A1), .Cout(full_adder_3_cout), .Cin(full_adder_4_cout), .Sum(S1));
  xor xor_4 (xor_4_out, Cin, B0);
  Full_adder full_adder_4 (.A(xor_4_out), .B(A0), .Cout(full_adder_4_cout), .Cin(Cin), .Sum(S0));
endmodule

module Full_adder (
  input  A,
  input  B,
  input  Cin,
  output Sum,
  output Cout
);

  wire and_1_out, and_2_out, xor_1_out;

  xor xor_1 (xor_1_out, A, B);
  xor xor_2 (Sum, xor_1_out, Cin);
  and and_1 (and_1_out, Cin, xor_1_out);
  and and_2 (and_2_out, B, A);
  or or_1 (Cout, and_1_out, and_2_out);
endmodule
