// Logisim project kmap-output.circ as structural Verilog
module OUT (
  input  Q0,
  input  Q1,
  input  Q2,
  input  Q3,
  output OUT
);

  wire not_1_out, not_2_out, not_3_out, not_4_out, or_1_out, or_2_out, or_3_out, or_4_out;

  or or_1 (or_1_out, Q2, Q3);
  not not_1 (not_1_out, Q2);
  or or_2 (or_2_out, not_1_out, not_2_out);
  not not_2 (not_2_out, Q3);
  or or_3 (or_3_out, Q0, not_3_out);
  not not_3 (not_3_out, Q1);
  not not_4 (not_4_out, Q0);
  or or_4 (or_4_out, not_4_out, Q1);
  and and_1 (OUT, or_1_out, or_2_out, or_3_out, or_4_out);
endmodule
