# Fritzing sketch 3.1.1 (saved by Fritzing 0.9.4)
breadboards: 2

parts:
  VCC1 = Battery
  S1 = SPST Switch [package=switch-spdt]
  S2 = SPST Switch [package=switch-spdt]
  S3 = Pushbutton [package="[THT]"]
  R1 = Resistor [tolerance=±5% resistance=220 package="1206 [SMD]"]
  7476 = IC, DIP package, 16 pins [chip_label=IC]
  7476_2 = IC, DIP package, 16 pins [chip_label=IC]
  U1 = SN74LS32N [package="DIP14 [THT]"]
  IC1 = 74HC08 Logic AND Gate [part_number=74HC08 package="DIP (Dual Inline) [THT]"]
  IC2 = 74HC08 Logic AND Gate [part_number=74HC08 package="DIP (Dual Inline) [THT]"]
  R2 = Resistor [tolerance=±5% resistance=220 package="1206 [SMD]"]
  LED1 = smd LED [color="Red (633nm)" package="1206 [SMD]"]
  R3 = Resistor [tolerance=±5% resistance=220 package="1206 [SMD]"]
  LED2 = smd LED [color="Red (633nm)" package="1206 [SMD]"]
  R4 = Resistor [tolerance=±5% resistance=220 package="1206 [SMD]"]
  R5 = Resistor [tolerance=±5% resistance=220 package="1206 [SMD]"]
  LED3 = smd LED [color="Red (633nm)" package="1206 [SMD]"]
  LED4 = smd LED [color="Red (633nm)" package="1206 [SMD]"]
  IC3 = 74HC08 Logic AND Gate [part_number=74HC08 package="DIP (Dual Inline) [THT]"]
  XOR = IC, DIP package, 14 pins [chip_label=IC]

nets:
  GND: VCC1.-, S1.O, S2.O, S3.Pin_3, S3.Pin_4, 7476.pin13, 7476_2.pin13, U1.GND, IC1.GND, IC2.GND, LED1.cathode, LED2.cathode, LED3.cathode, LED4.cathode, IC3.GND, XOR.pin7
  VCC: VCC1.+, S1.S, S2.S, R1.Pin_1, 7476.pin4, 7476.pin5, 7476.pin9, 7476.pin12, 7476.pin16, 7476_2.pin4, 7476_2.pin5, 7476_2.pin9, 7476_2.pin12, 7476_2.pin16, U1.Vcc, IC1.VCC, IC2.VCC, IC3.VCC, XOR.pin14
  N1: S1.P, IC1.2B, IC1.3A, IC2.2B, IC2.3A, XOR.pin13
  N2: S2.P, IC1.1B, IC1.4A, IC2.1B, IC2.4A, XOR.pin12
  N3: S3.Pin_1, S3.Pin_2, R1.Pin_0, IC3.3B
  N4: 7476.pin1, U1.1Y
  N5: 7476.pin6, U1.2Y
  N6: 7476.pin10, IC2.2A
  N7: 7476.pin11, IC2.1A, R3.Pin_1
  N8: 7476.pin14, IC1.2A
  N9: 7476.pin15, IC1.1A, R2.Pin_1
  N10: 7476_2.pin1, IC3.3Y
  N11: 7476_2.pin6, U1.3Y
  N12: 7476_2.pin10, IC2.3B
  N13: 7476_2.pin11, IC2.4B, R5.Pin_1
  N14: 7476_2.pin14, IC1.3B
  N15: 7476_2.pin15, IC1.4B, R4.Pin_1
  N16: U1.1A, IC1.1Y
  N17: U1.1B, IC1.2Y
  N18: U1.2A, IC2.1Y
  N19: U1.2B, IC2.2Y
  N20: U1.3A, IC2.3Y
  N21: U1.3B, IC2.4Y
  N22: U1.4A, IC1.3Y
  N23: U1.4B, IC1.4Y
  N24: R2.Pin_0, LED1.anode
  N25: R3.Pin_0, LED2.anode
  N26: R4.Pin_0, LED3.anode
  N27: R5.Pin_0, LED4.anode
  N28: IC3.3A, XOR.pin11
