# Fritzing sketch 3.1.2 (saved by Fritzing 0.9.4)
breadboards: 4

parts:
  VCC1 = Battery
  S1 = SPST Switch [package=switch-spdt]
  S2 = SPST Switch [package=switch-spdt]
  S3 = Pushbutton [package="[THT]"]
  R1 = Resistor [tolerance=±5% resistance=220 package="1206 [SMD]"]
  7476 = IC, DIP package, 16 pins [chip_label=IC]
  7476_2 = IC, DIP package, 16 pins [chip_label=IC]
  U1 = SN74LS32N [package="DIP14 [THT]"]
  IC1 = 74HC08 Logic AND Gate [part_number=74HC08 package="DIP (Dual Inline) [THT]"]
  IC2 = 74HC08 Logic AND Gate [part_number=74HC08 package="DIP (Dual Inline) [THT]"]
  R2 = Resistor [tolerance=±5% resistance=220 package="1206 [SMD]"]
  LED1 = smd LED [color="Red (633nm)" package="1206 [SMD]"]
  R3 = Resistor [tolerance=±5% resistance=220 package="1206 [SMD]"]
  LED2 = smd LED [color="Red (633nm)" package="1206 [SMD]"]
  R4 = Resistor [tolerance=±5% resistance=220 package="1206 [SMD]"]
  R5 = Resistor [tolerance=±5% resistance=220 package="1206 [SMD]"]
  LED3 = smd LED [color="Red (633nm)" package="1206 [SMD]"]
  LED4 = smd LED [color="Red (633nm)" package="1206 [SMD]"]
  IC3 = 74HC08 Logic AND Gate [part_number=74HC08 package="DIP (Dual Inline) [THT]"]
  XOR = IC, DIP package, 14 pins [chip_label=IC]
  IC4 = 74HC08 Logic AND Gate [part_number=74HC08 package="DIP (Dual Inline) [THT]"]
  IC5 = 74HC08 Logic AND Gate [part_number=74HC08 package="DIP (Dual Inline) [THT]"]
  U2 = 74HC04_HEX_INVERTER [package=dil14]
  S4 = SPST Switch [package=switch-spdt]
  S5 = SPST Switch [package=switch-spdt]
  S6 = SPST Switch [package=switch-spdt]
  S7 = SPST Switch [package=switch-spdt]
  U3 = 74HC04_HEX_INVERTER [package=dil14]
  IC6 = 74HC08 Logic AND Gate [part_number=74HC08 package="DIP (Dual Inline) [THT]"]
  U4 = 74HC04_HEX_INVERTER [package=dil14]
  IC7 = 74HC08 Logic AND Gate [part_number=74HC08 package="DIP (Dual Inline) [THT]"]

nets:
  GND: VCC1.-, S1.O, S2.O, S3.Pin_3, S3.Pin_4, 7476.pin13, 7476_2.pin13, U1.GND, IC1.GND, IC2.GND, LED1.cathode, LED2.cathode, LED3.cathode, LED4.cathode, IC3.GND, XOR.pin7, IC4.GND, IC5.GND, U2.GND, S4.S, S5.S, S6.S, S7.S, U3.GND, IC6.GND, U4.GND, IC7.GND
  VCC: VCC1.+, S1.S, S2.S, R1.Pin_1, 7476.pin4, 7476.pin5, 7476.pin9, 7476.pin12, 7476.pin16, 7476_2.pin4, 7476_2.pin5, 7476_2.pin9, 7476_2.pin12, 7476_2.pin16, U1.Vcc, IC1.VCC, IC2.VCC, IC3.VCC, XOR.pin14, IC4.VCC, IC5.VCC, U2.VCC, S4.O, S5.O, S6.O, S7.O, U3.VCC, IC6.VCC, U4.VCC, IC7.VCC
  N1: S1.P, U2.4A, IC7.1B
  N2: S2.P, U2.5A, IC7.4B
  N3: S3.Pin_1, S3.Pin_2, R1.Pin_0, IC3.2A
  N4: 7476.pin1, U1.1Y
  N5: 7476.pin2, IC4.4Y, U3.2A
  N6: 7476.pin3, U3.3Y
  N7: 7476.pin6, U1.2Y
  N8: 7476.pin7, U4.6Y
  N9: 7476.pin8, U4.4Y
  N10: 7476.pin10, IC2.2A
  N11: 7476.pin11, IC2.1A, R3.Pin_1
  N12: 7476.pin14, IC1.2A
  N13: 7476.pin15, IC1.1A, R2.Pin_1
  N14: 7476_2.pin1, IC3.2Y
  N15: 7476_2.pin2, U3.6Y
  N16: 7476_2.pin3, U3.5Y
  N17: 7476_2.pin6, U1.3Y
  N18: 7476_2.pin7, U3.4Y
  N19: 7476_2.pin8, U3.1Y
  N20: 7476_2.pin10, IC2.3B
  N21: 7476_2.pin11, IC2.4B, R5.Pin_1
  N22: 7476_2.pin14, IC1.3B
  N23: 7476_2.pin15, IC1.4B, R4.Pin_1
  N24: U1.1A, IC1.1Y
  N25: U1.1B, IC1.2Y
  N26: U1.2A, IC2.1Y
  N27: U1.2B, IC2.2Y
  N28: U1.3A, IC2.3Y
  N29: U1.3B, IC2.4Y
  N30: U1.4A, IC1.3Y
  N31: U1.4B, IC1.4Y
  N32: IC1.1B, IC1.4A, IC2.1B, IC2.4A, XOR.pin12, IC7.1Y
  N33: IC1.2B, IC1.3A, IC2.2B, IC2.3A, XOR.pin13, IC7.2Y
  N34: R2.Pin_0, LED1.anode
  N35: R3.Pin_0, LED2.anode
  N36: R4.Pin_0, LED3.anode
  N37: R5.Pin_0, LED4.anode
  N38: IC3.2B, XOR.pin11
  N39: IC4.1A, U2.1A, S5.P
  N40: IC4.1B, IC4.2B, IC4.3A, IC4.4A, IC5.1B, IC5.2B, IC5.3A, IC5.4A, IC7.4Y
  N41: IC4.1Y, U3.6A
  N42: IC4.2A, U2.1Y
  N43: IC4.2Y, U3.5A
  N44: IC4.3Y, U3.3A
  N45: IC4.3B, U2.3Y
  N46: IC4.4B, U2.3A, S6.P
  N47: IC5.1A, U2.2A, S4.P
  N48: IC5.1Y, U3.4A
  N49: IC5.2A, U2.2Y
  N50: IC5.2Y, U3.1A
  N51: IC5.3Y, U4.4A
  N52: IC5.3B, U2.6Y
  N53: IC5.4Y, U4.6A
  N54: IC5.4B, U2.6A, S7.P
  N55: U2.4Y, IC7.2B, IC7.4A
  N56: U2.5Y, IC7.1A, IC7.2A
