# Fritzing sketch Part 2 (saved by Fritzing 0.9.4)
breadboards: 1

parts:
  LED2 = smd LED [color="Red (633nm)" package="0805 [SMD]"]
  R4 = Resistor [tolerance=±5% resistance=220 package="0603 [SMD]"]
  VCC1 = Battery
  S1 = Pushbutton [package="[THT]"]
  R5 = Resistor [tolerance=±5% resistance=220 package="0603 [SMD]"]
  R6 = Resistor [tolerance=±5% resistance=220 package="0603 [SMD]"]
  S3 = SPST Switch [package=switch-spdt_lock.007s]
  74LS1 = 74LS73 [package="DIP (Dual Inline) [THT]"]
  74LS2 = 74LS73 [package="DIP (Dual Inline) [THT]"]
  U1 = 4070 4 x 2 Input XOR Gate, single part [part_number=4070 package="DIP (Dual Inline) [THT]"]
  R7 = Resistor [tolerance=±5% resistance=220 package="0603 [SMD]"]
  LED5 = smd LED [color="Red (633nm)" package="0805 [SMD]"]
  R8 = Resistor [tolerance=±5% resistance=220 package="0603 [SMD]"]
  LED6 = smd LED [color="Red (633nm)" package="0805 [SMD]"]
  U2 = SN74LS32N [package="DIP14 [THT]"]

nets:
  GND: LED2.cathode, VCC1.-, S1.Pin_1, S1.Pin_2, R5.Pin_0, S3.S, 74LS2.1CP, 74LS2.2CP, 74LS2.2J, 74LS2.GND, U1.GND, U1.Q4, LED5.cathode, LED6.cathode, U2.GND
  N1: LED2.anode, R4.Pin_1
  N2: R4.Pin_0, 74LS2.1Q, U1.B4
  VCC: VCC1.+, R5.Pin_1, R6.Pin_1, 74LS2.1K, 74LS2.Vcc, 74LS2.1J, U1.VDD, U2.Vcc
  N3: S1.Pin_3, S1.Pin_4
  N4: R6.Pin_0, S3.O, U1.B1, U1.B2, U1.A4
  N5: 74LS1.1K, 74LS1.1J, U2.1Y
  N6: 74LS1.1Q, R8.Pin_0
  N7: 74LS2.2Q', U1.A1
  N8: 74LS2.2Q, R7.Pin_0
  N9: 74LS2.1Q', U1.A2
  N10: U1.Q1, U2.1A
  N11: U1.Q2, U2.1B
  N12: R7.Pin_1, LED5.anode
  N13: R8.Pin_1, LED6.anode

notes:
  Yellow: Clock pulse
  Gray: X input
  Green: Q
  Blue: Q'

custom parts:
  74LS73: This device contains two independent negative-edge-trig gered J-K flip-flops with complementary outputs. The J and K data is processed by the flip-flops on the falling edge of the clock pulse. The clock triggering occurs at a voltage level and is not directly related to the transition time of the negative going edge of the clock pulse. The data on the J and K inputs is allowed to change while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
