# Fritzing sketch PishGoz3-3frit (saved by Fritzing 0.9.4)
breadboards: 3

parts:
  VCC1 = Battery
  S1 = Momentary Switch [package=tactile-pth]
  S2 = Momentary Switch [package=tactile-pth]
  S3 = Momentary Switch [package=tactile-pth]
  S4 = Momentary Switch [package=tactile-pth]
  S5 = Momentary Switch [package=tactile-pth]
  S6 = Momentary Switch [package=tactile-pth]
  S7 = Momentary Switch [package=tactile-pth]
  S8 = Momentary Switch [package=tactile-pth]
  S9 = Momentary Switch [package=tactile-pth]
  S10 = Momentary Switch [package=tactile-pth]
  7_Segment1 = 7 Segment Display
  U1 = SN74LS32N [package="DIP14 [THT]"]
  U2 = SN74LS32N [package="DIP14 [THT]"]
  U3 = SN74LS32N [package="DIP14 [THT]"]
  U4 = SN74LS32N [package="DIP14 [THT]"]
  U6 = SN74LS32N [package="DIP14 [THT]"]
  U7 = SN74LS32N [package="DIP14 [THT]"]
  U8 = SN74LS32N [package="DIP14 [THT]"]
  U9 = SN74LS32N [package="DIP14 [THT]"]
  7_Segment2 = 7 Segment Display
  S11 = SWITCH-MOMENTARY-2 [package=tactile-pth]
  U10 = SN74LS32N [package="DIP14 [THT]"]
  U11 = SN74LS32N [package="DIP14 [THT]"]
  U12 = SN74LS32N [package="DIP14 [THT]"]
  U13 = SN74LS20N [package="DIP14 [THT]"]
  U14 = SN74LS20N [package="DIP14 [THT]"]

nets:
  GND: VCC1.-, 7_Segment1.Segment_DP, U1.GND, U2.GND, U3.GND, U4.GND, U6.2Y, U7.2Y, U8.GND, U9.GND, 7_Segment2.Segment_DP, U10.GND
  VCC: VCC1.+, S1.3, S2.3, S3.3, S4.3, S5.3, S6.3, S7.3, S8.3, S9.3, S10.3, U1.Vcc, U2.Vcc, U3.Vcc, U4.Vcc, U8.2B, U8.2Y, U9.2B, U9.2Y, S11.2, U10.Vcc, U14.VCC
  N1: S2.1, U1.3Y
  N2: S3.1, U2.3Y
  N3: S4.1, U2.4Y
  N4: S5.1, U1.4Y
  N5: S6.2, U2.1A
  N6: S7.2, U2.2A
  N7: S8.2, U1.1A
  N8: S9.2, U1.2A
  N9: 7_Segment1.Segment_E, U9.3Y
  N10: 7_Segment1.Segment_D, U9.3A
  N11: 7_Segment1.Segment_C, U9.3B
  N12: 7_Segment1.Segment_B, U9.4Y
  N13: 7_Segment1.Segment_A, U9.4A
  N14: 7_Segment1.Segment_F, U9.4B
  N15: 7_Segment1.Segment_G, U9.Vcc
  N16: U1.1B, U1.2B, U1.3A, U1.4A, U2.1B, U14.1A
  N17: U1.1Y, U3.1A
  N18: U1.2Y, U3.2A
  N19: U1.3B, U3.3Y
  N20: U1.4B, U3.4Y
  N21: U2.1Y, U4.1A
  N22: U2.2B, U2.3A, U2.4A, U12.1Y, U13.1A, U14.1B
  N23: U2.2Y, U4.2A
  N24: U2.3B, U4.3Y
  N25: U2.4B, U4.4Y
  N26: U3.1B, U3.2B, U3.3A, U3.4A, U4.1B, U4.2B, U4.3A, U4.4A, U13.1B
  N27: U3.1Y, U7.3Y
  N28: U3.2Y, U7.4Y
  N29: U3.3B, U6.1A
  N30: U3.4B, U6.4Y
  N31: U4.1Y, U7.1A
  N32: U4.2Y, U7.2A
  N33: U4.3B, U6.2A
  N34: U4.4B, U6.3Y
  N35: U6.1B, U8.1A, U10.3A
  N36: U6.1Y, S11.1
  N37: U6.2B, U8.1B, U11.4Y
  N38: U6.3A, U8.1Y, U11.3B
  N39: U6.4A, U8.2A, U10.3Y
  N40: U6.4B, U7.1Y
  N41: U7.1B, U9.1A, U10.4A
  N42: U7.2B, U9.1B, U10.4Y
  N43: U7.3A, U9.1Y, U11.3A
  N44: U7.4A, U9.2A, U10.3B
  N45: U8.3Y, 7_Segment2.Segment_E
  N46: U8.3A, 7_Segment2.Segment_D
  N47: U8.3B, 7_Segment2.Segment_C
  N48: U8.4Y, 7_Segment2.Segment_B
  N49: U8.4A, 7_Segment2.Segment_A
  N50: U8.4B, 7_Segment2.Segment_F
  N51: U8.Vcc, 7_Segment2.Segment_G
  N52: U10.4B, U12.1A
  N53: U11.4A, U12.1B
