# Fritzing sketch Az4 (saved by Fritzing 0.9.4)
breadboards: 5

parts:
  VCC1 = Battery
  S1 = SPST Switch [package=switch-spdt]
  S2 = Momentary Switch [package=ksa_sealed_tac_switch]
  S3 = Momentary Switch [package=ksa_sealed_tac_switch]
  R1 = Resistor [tolerance=±5% resistance=220 package="1206 [SMD]"]
  R2 = Resistor [tolerance=±5% resistance=220 package="1206 [SMD]"]
  U1 = 74HC04_HEX_INVERTER [package=dil14]
  IC1 = IC, DIP package, 14 pins [chip_label=7474]
  IC2 = IC, DIP package, 14 pins [chip_label=7474]
  74190 = IC, DIP package, 16 pins [chip_label=74190]
  74190_2 = IC, DIP package, 16 pins [chip_label=74190]
  IC3 = 74HC08 Logic AND Gate [part_number=74HC08 package="DIP (Dual Inline) [THT]"]
  IC4 = 74HC08 Logic AND Gate [part_number=74HC08 package="DIP (Dual Inline) [THT]"]
  IC5 = 74HC08 Logic AND Gate [part_number=74HC08 package="DIP (Dual Inline) [THT]"]
  IC6 = 74HC08 Logic AND Gate [part_number=74HC08 package="DIP (Dual Inline) [THT]"]
  U2 = SN74LS32N [package="DIP14 [THT]"]
  U3 = SN74LS32N [package="DIP14 [THT]"]
  U4 = SN74LS32N [package="DIP14 [THT]"]
  IC7 = DIP - 14 pins [chip_label=74LS86 package="DIP (Dual Inline) [THT]"]
  IC8 = 74HC08 Logic AND Gate [part_number=74HC08 package="DIP (Dual Inline) [THT]"]
  U5 = SN74LS32N [package="DIP14 [THT]"]
  IC9 = 74HC08 Logic AND Gate [part_number=74HC08 package="DIP (Dual Inline) [THT]"]
  IC10 = 74HC08 Logic AND Gate [part_number=74HC08 package="DIP (Dual Inline) [THT]"]
  IC11 = 74HC08 Logic AND Gate [part_number=74HC08 package="DIP (Dual Inline) [THT]"]
  IC12 = 74HC08 Logic AND Gate [part_number=74HC08 package="DIP (Dual Inline) [THT]"]
  U6 = SN74LS32N [package="DIP14 [THT]"]
  R3 = Resistor [tolerance=±5% resistance=220 package="1206 [SMD]"]
  LED1 = smd LED [color="Red (633nm)" package="1206 [SMD]"]
  R4 = Resistor [tolerance=±5% resistance=220 package="1206 [SMD]"]
  LED2 = smd LED [color="Red (633nm)" package="1206 [SMD]"]
  R5 = Resistor [tolerance=±5% resistance=220 package="1206 [SMD]"]
  LED3 = smd LED [color="Red (633nm)" package="1206 [SMD]"]
  R9 = Resistor [tolerance=±5% resistance=220 package="1206 [SMD]"]
  LED4 = smd LED [color="Red (633nm)" package="1206 [SMD]"]
  R10 = Resistor [tolerance=±5% resistance=220 package="1206 [SMD]"]
  LED5 = smd LED [color="Red (633nm)" package="1206 [SMD]"]
  LED6 = smd LED [color="Red (633nm)" package="1206 [SMD]"]
  R11 = Resistor [tolerance=±5% resistance=220 package="1206 [SMD]"]
  R12 = Resistor [tolerance=±5% resistance=220 package="1206 [SMD]"]
  R13 = Resistor [tolerance=±5% resistance=220 package="1206 [SMD]"]
  R14 = Resistor [tolerance=±5% resistance=220 package="1206 [SMD]"]
  R15 = Resistor [tolerance=±5% resistance=220 package="1206 [SMD]"]
  LED7 = smd LED [color="Red (633nm)" package="1206 [SMD]"]
  LED8 = smd LED [color="Red (633nm)" package="1206 [SMD]"]
  LED9 = smd LED [color="Red (633nm)" package="1206 [SMD]"]
  LED10 = smd LED [color="Red (633nm)" package="1206 [SMD]"]
  S4 = Momentary Switch [package=ksa_sealed_tac_switch]
  R16 = Resistor [tolerance=±5% resistance=220 package="1206 [SMD]"]

nets:
  GND: VCC1.-, S1.S, S2.1, S3.1, U1.GND, IC1.pin7, IC2.pin7, 74190.pin1, 74190.pin4, 74190.pin8, 74190.pin9, 74190.pin10, 74190.pin15, 74190_2.pin1, 74190_2.pin4, 74190_2.pin8, 74190_2.pin9, 74190_2.pin10, 74190_2.pin15, IC3.GND, IC4.GND, IC5.GND, IC6.GND, U2.GND, U3.GND, U4.GND, IC7.GND, IC8.GND, U5.GND, IC9.GND, IC10.GND, IC11.GND, IC12.GND, U6.GND, LED1.cathode, R4.Pin_1, LED2.cathode, LED3.cathode, LED5.cathode, LED6.cathode, LED7.cathode, LED8.cathode, LED9.cathode, LED10.cathode, S4.2
  VCC: VCC1.+, S1.O, R1.Pin_0, R2.Pin_0, U1.VCC, IC1.pin14, IC2.pin14, 74190.pin16, 74190_2.pin16, IC3.VCC, IC4.VCC, IC5.VCC, IC6.VCC, U2.Vcc, U3.Vcc, U4.Vcc, IC7.VCC, IC8.VCC, U5.Vcc, IC9.VCC, IC10.VCC, IC11.VCC
  N1: S1.P, IC3.4B, IC8.4B, IC10.4B
  N2: S2.3, R1.Pin_1, U1.6A, IC4.3A, IC4.4A, U4.1Y, IC10.4A
  N3: S3.2, R16.Pin_0
  N4: S3.3, R2.Pin_1, U1.1A
  N5: U1.1Y, IC1.pin13, IC2.pin1, IC2.pin13, 74190.pin11, 74190_2.pin11
  N6: U1.2A, IC12.2Y
  N7: U1.2Y, IC1.pin2
  N8: U1.3A, IC12.4Y
  N9: U1.3Y, 74190.pin14
  N10: U1.4Y, 74190_2.pin5
  N11: U1.4A, 74190.pin7, U3.1B, R11.Pin_0
  N12: U1.6Y, IC1.pin1, IC9.1B, U6.2A
  N13: IC1.pin3, IC1.pin11, IC2.pin3, IC2.pin11, S4.4, R16.Pin_1
  N14: IC1.pin5, 74190.pin5
  N15: IC1.pin8, IC3.1A, IC3.4A, IC12.2A, IC12.4B
  N16: IC1.pin9, IC8.4A, U5.1A, IC9.1A, IC10.1A, IC12.1A, U6.1A
  N17: IC1.pin12, U2.1Y
  N18: IC2.pin2, U5.3Y
  N19: IC2.pin5, IC3.1B, IC7.B4, IC9.2B, IC9.4B, IC10.1B, IC12.1B
  N20: IC2.pin6, IC3.3A, IC8.3B
  N21: IC2.pin8, IC3.2B, IC8.3A
  N22: IC2.pin9, IC7.A4, IC10.2B, IC12.2B, IC12.4A, U6.4A
  N23: IC2.pin10, IC9.4A
  N24: IC2.pin12, U5.2Y
  N25: 74190.pin2, U3.4B, R9.Pin_0
  N26: 74190.pin3, U3.4A, R5.Pin_0
  N27: 74190.pin6, U3.1A, R10.Pin_0
  N28: 74190.pin13, 74190_2.pin14
  N29: 74190_2.pin2, U3.2A, R12.Pin_0
  N30: 74190_2.pin3, U3.2B, R13.Pin_0
  N31: 74190_2.pin6, U4.4B, R14.Pin_0
  N32: 74190_2.pin7, U4.4A, R15.Pin_0
  N33: IC3.1Y, IC3.2A
  N34: IC3.2Y, U2.4A
  N35: IC3.3Y, IC4.4B
  N36: IC3.3B, IC3.4Y
  N37: IC4.3Y, U2.3A
  N38: IC4.3B, IC7.Y4, U6.1B
  N39: IC4.4Y, U2.4B
  N40: U2.1A, U2.3Y
  N41: U2.1B, IC8.1Y, U5.3A, U5.3B, U5.4B
  N42: U2.3B, U2.4Y
  N43: U3.1Y, U3.3A
  N44: U3.2Y, U4.3A
  N45: U3.3Y, U4.1A
  N46: U3.3B, U3.4Y
  N47: U4.1B, U4.3Y
  N48: U4.3B, U4.4Y
  N49: IC8.1A, IC8.4Y
  N50: IC8.1B, IC8.3Y
  N51: U5.1B, IC10.3Y
  N52: U5.1Y, U5.2A
  N53: U5.2B, IC10.2Y
  N54: U5.4Y, U5.4A, IC9.2Y
  N55: IC9.1Y, IC9.2A
  N56: IC9.3B, IC9.4Y
  N57: IC10.1Y, IC10.3A
  N58: IC10.2A, IC10.3B, IC10.4Y
  N59: IC12.1Y, U6.4B
  VCC_2: IC12.VCC, U6.Vcc, LED4.cathode, S4.1
  N60: U6.1Y, R3.Pin_0
  N61: U6.4Y, R4.Pin_0
  N62: R3.Pin_1, LED1.anode
  N63: R5.Pin_1, LED3.anode
  N64: R9.Pin_1, LED4.anode
  N65: R10.Pin_1, LED5.anode
  N66: LED6.anode, R11.Pin_1
  N67: R12.Pin_1, LED8.anode
  N68: R13.Pin_1, LED7.anode
  N69: R14.Pin_1, LED9.anode
  N70: R15.Pin_1, LED10.anode

custom parts:
  DIP - 14 pins: A DIP stand-in part for whatever IC you want. With 14 pins on a 300mil dual inline package (DIP) footprint.
