# Fritzing sketch part 1 (saved by Fritzing 0.9.4)
breadboards: 4

parts:
  VCC1 = Battery
  IC1 = 74HC08 Logic AND Gate [part_number=74HC08 package="DIP (Dual Inline) [THT]"]
  U1 = 74HC04_HEX_INVERTER [package=dil14]
  SW1 = DIP Switch 8 Position [package=dipswitch-08]
  R1 = Resistor [tolerance=±5% resistance=220 package="1206 [SMD]"]
  R2 = Resistor [tolerance=±5% resistance=220 package="1206 [SMD]"]
  R3 = Resistor [tolerance=±5% resistance=220 package="1206 [SMD]"]
  R4 = Resistor [tolerance=±5% resistance=220 package="1206 [SMD]"]
  R5 = Resistor [tolerance=±5% resistance=220 package="1206 [SMD]"]
  R6 = Resistor [tolerance=±5% resistance=220 package="1206 [SMD]"]
  R7 = Resistor [tolerance=±5% resistance=220 package="1206 [SMD]"]
  U3 = 4070 4 x 2 Input XOR Gate, single part [part_number=4070 package="DIP (Dual Inline) [THT]"]
  U5 = SN74LS20N [package="DIP14 [THT]"]
  U6 = SN74LS21N [package="DIP14 [THT]"]
  U7 = SN74LS32N [package="DIP14 [THT]"]
  U8 = Quad Comparator [part_number=LM239 package="DIP (Dual Inline) [THT]"]
  part = LM239 [part_number=LM239]  # not connected
  U8_1 = LM239 [part_number=LM239]  # not connected
  U8_2 = LM239 [part_number=LM239]  # not connected
  U8_3 = LM239 [part_number=LM239]  # not connected
  U8_4 = LM239 [part_number=LM239]  # not connected
  IC2 = SELECTOR_MULTIPLEXER [package=dil16]
  VCC2 = Battery
  IC3 = SELECTOR_MULTIPLEXER [package=dil16]
  U9 = 74HC04_HEX_INVERTER [package=dil14]
  U10 = 74HC04_HEX_INVERTER [package=dil14]
  74HC139N1 = 74HC139N [part_number=74HC139N package="DIP (Dual Inline) [THT]"]
  74HC139N2 = 74HC139N [part_number=74HC139N package="DIP (Dual Inline) [THT]"]
  VCC3 = Battery
  LED1 = smd LED [color="Red (633nm)" package="0805 [SMD]"]
  LED2 = smd LED [color="Red (633nm)" package="0805 [SMD]"]
  LED3 = smd LED [color="Red (633nm)" package="0805 [SMD]"]
  LED4 = smd LED [color="Red (633nm)" package="0805 [SMD]"]
  R8 = Resistor [tolerance=±5% resistance=220 package="1206 [SMD]"]
  R9 = Resistor [tolerance=±5% resistance=220 package="1206 [SMD]"]
  R10 = Resistor [tolerance=±5% resistance=220 package="1206 [SMD]"]
  R11 = Resistor [tolerance=±5% resistance=220 package="1206 [SMD]"]
  LED5 = smd LED [color="Red (633nm)" package="0805 [SMD]"]
  LED6 = smd LED [color="Red (633nm)" package="0805 [SMD]"]
  LED7 = smd LED [color="Red (633nm)" package="0805 [SMD]"]
  LED8 = smd LED [color="Red (633nm)" package="0805 [SMD]"]
  R12 = Resistor [tolerance=±5% resistance=220 package="1206 [SMD]"]
  R13 = Resistor [tolerance=±5% resistance=220 package="1206 [SMD]"]
  R14 = Resistor [tolerance=±5% resistance=220 package="1206 [SMD]"]
  R15 = Resistor [tolerance=±5% resistance=220 package="1206 [SMD]"]

nets:
  GND: VCC1.-, IC1.GND, U1.GND, SW1.6, SW1.7, SW1.8, U3.GND, U5.GND, U6.GND, U7.GND, U8.connector4, U8.connector6, U8.connector8
  VCC: VCC1.+, IC1.VCC, U1.VCC, R1.Pin_0, R2.Pin_0, R3.Pin_0, R4.Pin_0, R5.Pin_0, R6.Pin_0, R7.Pin_0, U3.VDD, U5.1D, U5.2A, U5.VCC, U6.1D, U6.2A, U6.2B, U6.VCC, U7.Vcc, U8.connector13
  N1: IC1.1A, IC1.4B, U1.4Y
  N2: IC1.1B, U3.Q1
  N3: IC1.1Y, U7.1A
  N4: IC1.2A, U1.6Y, U6.2D, U8.connector3
  N5: IC1.2B, U1.4A, SW1.9, R3.Pin_1, U5.1C, U5.2B, U6.1C, U8.connector1, U8.connector9
  N6: IC1.2Y, U7.1B, U7.4B
  N7: IC1.4A, U6.2Y, U9.2A
  N8: U1.1A, U8.connector7
  N9: U1.1Y, IC3.A_3Y
  N10: U1.5Y, U5.1B
  N11: U1.5A, SW1.10, R2.Pin_1, U3.B1, U5.2C, U6.1B, U6.2C, U8.connector0, U8.connector11
  N12: U1.6A, SW1.11, R1.Pin_1, U5.1A, U5.2D, U6.1A, U8.connector12
  N13: SW1.13, R7.Pin_1, IC2.A_1Y, IC3.A_1Y
  N14: SW1.14, R6.Pin_1, IC2.A_1B, IC3.A_1B
  N15: SW1.15, R5.Pin_1, IC2.A_1A, IC3.A_1A
  N16: SW1.16, R4.Pin_1, IC2.A_!A!_B, IC3.A_!A!_B
  N17: U5.1Y, U9.1A
  N18: U5.2Y, U9.3A
  N19: U6.1Y, U7.4A
  N20: U7.1Y, U9.1Y
  N21: U7.4Y, U9.2Y
  N22: U8.connector5, IC2.A_3Y
  N23: IC2.A_2B, U10.3A
  N24: IC2.A_2Y, U10.3Y
  N25: IC2.P_GND, VCC2.-, IC3.P_GND, R12.Pin_0, R13.Pin_0, R15.Pin_0
  N26: IC2.A_3B, U10.2Y
  N27: IC2.A_3A, U10.2A
  N28: IC2.A_4Y, 74HC139N1.1Y0, LED4.anode
  N29: IC2.A_4B, 74HC139N1.1B, LED2.anode
  N30: IC2.A_4A, 74HC139N1.1A, LED3.anode
  N31: IC2.A_G, 74HC139N1.1G_
  N32: IC2.P_VCC, VCC2.+, IC3.P_VCC
  N33: IC3.A_2B, U10.6A, 74HC139N2.2B, LED8.anode
  N34: IC3.A_2Y, U10.VCC, 74HC139N2.2Y0, LED6.anode
  N35: IC3.A_3B, U9.4Y, 74HC139N2.2A, LED7.anode
  N36: IC3.A_3A, U9.4A, 74HC139N2.2G_, LED5.anode
  N37: IC3.A_4Y, 74HC139N2.1B
  N38: IC3.A_4B, 74HC139N2.1Y0
  N39: IC3.A_4A, 74HC139N2.1A
  N40: IC3.A_G, 74HC139N2.1G_
  N41: U9.5Y, 74HC139N1.2Y0
  N42: U9.5A, 74HC139N1.2B
  N43: U9.6Y, 74HC139N1.2A
  N44: U9.6A, 74HC139N1.2G_
  VCC_2: U9.VCC, 74HC139N1.VCC, 74HC139N2.VCC, VCC3.+
  GND_2: U10.GND, 74HC139N1.GND, 74HC139N2.GND, VCC3.-, R8.Pin_0, R9.Pin_0, R10.Pin_0, R11.Pin_0
  N45: LED1.cathode, R8.Pin_1
  N46: LED2.cathode, R10.Pin_1
  N47: LED3.cathode, R9.Pin_1
  N48: LED4.cathode, R11.Pin_1
  N49: LED5.cathode, R12.Pin_1
  N50: LED6.cathode, R13.Pin_1
  N51: LED7.cathode, R14.Pin_1
  N52: LED8.cathode, R15.Pin_1

notes:
  24: U10: S3
  25: U16: M
  46: U17: S2
  47: U20: S0
  38: U40: S1
  23: U14: A mux
  22: U15: B mux
  black: M0 M1 M2
  red: inverted Ms
  تراشه 7486 یافت نشد، از 4070 استفاده شد
  LM239:
  به جای
  4-input OR
  قطعه ALU یافت نشد، به جای آن دو عدد hex inverter گذاشته شد
  به جای 4 عدد d-ff
  دو قطعه 74HC139N
  گذاشته شد
  بخش کنترلر کاملا درست طراحی شده اما بخش بالایی به دلیل نبود اکثر قطعات
  ممکن است دارای اشتباه برای جایگاه پایه ها باشد.
